# Fritzing sketch c64 internal saver R1.2 (saved by Fritzing 0.9.3b)
circuit board: 5cm x 5cm

parts:
  R1 = Resistor [tolerance=±5% resistance=470 package=THT]
  R2 = Resistor [tolerance=±5% resistance=470 package=THT]
  R3 = Resistor [tolerance=±5% resistance=2.2k package=THT]
  R4 = Resistor [tolerance=±5% resistance=470 package=THT]
  R5 = Resistor [tolerance=±5% resistance=470 package=THT]
  Fuse1 = Fuse with Handler [part_number=Htc-15m]
  LEDG = female pin header, 2 pins [form="♀ (female)"]
  LEDR = female pin header, 2 pins [form="♀ (female)"]
  D2 = Rectifier Diode [part_number=1N4001 package="300 mil [THT]"]
  D1 = Zener Diode [part_number=1N4732A breakdown_voltage=4.7V package="300 mil [THT]"]
  J1 = female pin header, 3 pins [form="♀ (female)"]
  RELAY = RELAY [package=relay-jzc]
  Q2 = NPN-Transistor [package="TO92 [THT]"]
  Q1 = NPN-Transistor [package="TO92 [THT]"]

nets:
  N1: R1.Pin_0, D1.anode, Q1.B
  N2: R1.Pin_1, LEDG.pin1, LEDR.pin1, J1.pin3, Q2.E, Q1.E
  N3: R2.Pin_0, R3.Pin_0, Fuse1.Connector2, D2.cathode, RELAY.MAIN, RELAY.COIL1
  N4: R2.Pin_1, D1.cathode
  N5: R3.Pin_1, Q2.B, Q1.C
  N6: R4.Pin_0, J1.pin2, RELAY.NO
  N7: R4.Pin_1, LEDG.pin2
  N8: R5.Pin_0, RELAY.NC
  N9: R5.Pin_1, LEDR.pin2
  N10: Fuse1.Connector1, J1.pin1
  N11: D2.anode, RELAY.COIL2, Q2.C

notes:
  Commodore C64
  Board by S.Orton
  REV 1.2 12/02/2020
  Circuit Designed by R. Carlsen
  For 250466 M/Board Cut L5 resistor or jumper and place module in series
  Internal Saver
  2A
  2 Amp
  GND
  5v IN
  5V OUT
  From resistor pad
  5v OUT
  Red LED to NO
  Green LED to NC
  In
  Out
  R1.1 Added Wiring Connector
  C64 Internal Saver, Over voltage protection circuit for 5v lines of Commodore 64 etc., 1.2
  R1.2 moved Wiring Connector to fit molex connectors on LED's
  C
  B
  E
  R1.2 Transistor pinout changed to CBE from EBC
  INPUT
  OUTPUT
